// Logisim project 1.circ as structural Verilog: 1 circuit, main circuit main
module main (
  input  in_1,
  input  in_2,
  input  in_3,
  input  in_4,
  output out_5,
  output out_6
);

  wire transistor_6_out, transistor_7_out, transistor_8_out;

  nand nand_1 (out_5, in_1, in_2, in_3, in_4);
  Transistor transistor_1 (.in(1'b1), .out(out_6), .gate(in_1));
  Transistor transistor_2 (.in(1'b1), .out(out_6), .gate(in_2));
  Transistor transistor_3 (.in(1'b1), .out(out_6), .gate(in_4));
  Transistor transistor_4 (.in(1'b1), .out(out_6), .gate(in_3));
  Transistor #(.\type ("n")) transistor_5 (.in(transistor_6_out), .out(out_6), .gate(in_1));
  Transistor #(.\type ("n")) transistor_6 (.in(transistor_7_out), .out(transistor_6_out), .gate(in_2));
  Transistor #(.\type ("n")) transistor_7 (.in(transistor_8_out), .out(transistor_7_out), .gate(in_3));
  Transistor #(.\type ("n")) transistor_8 (.in(1'b0), .out(transistor_8_out), .gate(in_4));
endmodule
