// Logisim project 2.circ as structural Verilog: 1 circuit, main circuit main
module main (
  input  in_1,
  input  in_2,
  input  in_3,
  input  in_4,
  output out_5,
  output out_6
);

  wire transistor_3_out, transistor_4_out, transistor_5_out;

  nor nor_1 (out_5, in_1, in_2, in_3, in_4);
  Transistor #(.\type ("n")) transistor_1 (.in(1'b0), .out(out_6), .gate(in_1));
  Transistor #(.\type ("n")) transistor_2 (.in(1'b0), .out(out_6), .gate(in_2));
  Transistor transistor_3 (.in(1'b1), .out(transistor_3_out), .gate(in_1));
  Transistor transistor_4 (.in(transistor_3_out), .out(transistor_4_out), .gate(in_2));
  Transistor transistor_5 (.in(transistor_4_out), .out(transistor_5_out), .gate(in_3));
  Transistor transistor_6 (.in(transistor_5_out), .out(out_6), .gate(in_4));
  Transistor #(.\type ("n")) transistor_7 (.in(1'b0), .out(out_6), .gate(in_3));
  Transistor #(.\type ("n")) transistor_8 (.in(1'b0), .out(out_6), .gate(in_4));
endmodule
