// Logisim project 1.circ as structural Verilog: 1 circuit, main circuit main
module main (
  input  a,
  input  b,
  input  c,
  output out_4
);

  wire na_out, nand_1_out, nand_2_out, nb_out, nc_out;

  not na (na_out, a);  // NAND_Gate
  not nb (nb_out, b);  // NAND_Gate
  not nc (nc_out, c);  // NAND_Gate
  nand nand_1 (nand_1_out, nb_out, c);
  nand nand_2 (nand_2_out, b, nc_out);
  nand nand_3 (out_4, nand_1_out, na_out, nand_2_out);
endmodule
