// Logisim project 2.circ as structural Verilog: 1 circuit, main circuit main
module main (
  input  a,
  input  b,
  input  c,
  output out_4
);

  wire na_out, nb_out, nc_out, nor_1_out, nor_2_out, nor_3_out;

  not na (na_out, a);  // NOR_Gate
  not nb (nb_out, b);  // NOR_Gate
  not nc (nc_out, c);  // NOR_Gate
  nor nor_1 (nor_1_out, b, nc_out);
  nor nor_2 (nor_2_out, nb_out, c);
  nor nor_3 (nor_3_out, nor_1_out, a, nor_2_out);
  not nor_4 (out_4, nor_3_out);  // NOR_Gate
endmodule
