// Logisim project 1.circ as structural Verilog: 1 circuit, main circuit main
module main (
  input  a,
  input  b,
  input  c,
  output out_4,
  output out_5,
  output out_6
);

  wire and_1_out, and_2_out, and_3_out, and_4_out, and_5_out, na_out, nb_out, nc_out;

  not na (na_out, a);
  not nb (nb_out, b);
  not nc (nc_out, c);
  and and_1 (and_1_out, nc_out, nc_out, b);
  and and_2 (and_2_out, nb_out, a);
  and and_3 (and_3_out, na_out, c);
  and and_4 (and_4_out, b, c);
  and and_5 (and_5_out, nb_out, nc_out);
  or or_1 (out_6, a, nc_out);
  or or_2 (out_4, and_3_out, and_2_out, and_1_out);
  or or_3 (out_5, and_5_out, and_4_out, a);
endmodule
