// Logisim project 2.circ as structural Verilog: 1 circuit, main circuit main
module main (
  input  a,
  input  b,
  input  c,
  output out_4
);

  wire and_1_out, and_2_out, na_out, nb_out, nc_out;

  not na (na_out, a);
  not nc (nc_out, c);
  not nb (nb_out, b);
  and and_1 (and_1_out, na_out, c);
  and and_2 (and_2_out, a, nc_out);
  or or_1 (out_4, and_2_out, and_1_out, nb_out);
endmodule
