// Logisim project 3-4.circ as structural Verilog: 1 circuit, main circuit ПОРА
module \ПОРА  (
  output a,
  output b,
  output c,
  output d,
  output e,
  output f,
  output g
);

  wire clock_2_out, not_1_out;

  Clock #(.highDuration(2), .lowDuration(2)) clock_1 (.out(g));
  Clock clock_2 (.out(clock_2_out));
  xor xor_1 (d, g, clock_2_out);
  not not_1 (not_1_out, g);
  or or_1 (e, not_1_out, clock_2_out);
  _7_Segment_Display u_7_segment_display_1 (.g(g), .f(e), .a(1'b1), .b(1'b1), .e(e), .d(d), .c(1'b1));  // open: dp

  assign a = 1'b1;
  assign b = 1'b1;
  assign c = 1'b1;
  assign f = e;

  // Notes on the sheet:
  //   X1
  //   X0
endmodule
