// Logisim project 1.circ as structural Verilog: 1 circuit, main circuit main
module main (
  input  CLK,
  input  T,
  output out_3,
  output out_4
);

  wire and_1_out, and_2_out, not_1_out, or_1_out;

  not not_1 (not_1_out, T);
  and and_1 (and_1_out, out_3, not_1_out);
  and and_2 (and_2_out, T, out_4);
  or or_1 (or_1_out, and_1_out, and_2_out);
  D_Flip_Flop d_ff_1 (.clk(CLK), .D(or_1_out), .Q(out_3), .Qn(out_4));  // open: preset, en, reset
endmodule
