// Logisim project 2.circ as structural Verilog: 1 circuit, main circuit main
module main (
  input  CLK,
  input  K,
  input  J,
  output out_4,
  output out_5
);

  wire and_1_out, and_2_out, not_1_out, or_1_out;

  not not_1 (not_1_out, K);
  and and_1 (and_1_out, out_4, not_1_out);
  and and_2 (and_2_out, J, out_5);
  or or_1 (or_1_out, and_1_out, and_2_out);
  D_Flip_Flop d_ff_1 (.clk(CLK), .D(or_1_out), .Q(out_4), .Qn(out_5));  // open: preset, en, reset
endmodule
