// Logisim project 3.circ as structural Verilog: 1 circuit, main circuit main
module main (
  input  CLK,
  input  D,
  output out_3,
  output out_4
);

  wire not_1_out;

  not not_1 (not_1_out, D);
  J_K_Flip_Flop j_k_ff_1 (.J(D), .clk(CLK), .K(not_1_out), .Q(out_3), .Qn(out_4));  // open: preset, en, reset
endmodule
