// Logisim project 4.circ as structural Verilog: 1 circuit, main circuit main
module main (
  input  CLK,
  input  T,
  output out_3,
  output out_4
);

  J_K_Flip_Flop j_k_ff_1 (.J(T), .clk(CLK), .K(T), .Q(out_3), .Qn(out_4));  // open: preset, en, reset
endmodule
