// Logisim project Pract7_1.circ as structural Verilog: 1 circuit, main circuit main
module main (
  input  CLK,
  input  X1,
  input  X0
);

  wire d_ff_1_q, d_ff_1_qn, d_ff_2_q, d_ff_2_qn, nand_1_out, nand_2_out, nand_3_out, nand_4_out, nand_5_out,
       nand_6_out, nand_7_out, nand_8_out, nand_9_out, nand_10_out, nand_11_out;

  nand nand_1 (nand_1_out, X1, X1);
  nand nand_2 (nand_2_out, X0, X0);
  nand nand_3 (nand_3_out, d_ff_1_qn, d_ff_2_qn);
  nand nand_4 (nand_4_out, d_ff_1_q, d_ff_2_q);
  nand nand_5 (nand_5_out, d_ff_1_qn, d_ff_2_q);
  nand nand_6 (nand_6_out, d_ff_1_qn, X1);
  nand nand_7 (nand_7_out, nand_1_out, d_ff_2_q);
  nand nand_8 (nand_8_out, nand_3_out, nand_4_out);
  nand nand_9 (nand_9_out, nand_5_out, nand_5_out);
  nand nand_10 (nand_10_out, d_ff_2_qn, nand_1_out);
  nand nand_11 (nand_11_out, nand_2_out, nand_6_out, nand_7_out);
  LED led_1 (.in(nand_8_out));
  LED led_2 (.in(nand_9_out));
  LED led_3 (.in(nand_10_out));
  LED led_4 (.in(nand_11_out));
  LED led_5 (.in(d_ff_1_q));
  D_Flip_Flop d_ff_1 (.clk(CLK), .D(nand_10_out), .Q(d_ff_1_q), .Qn(d_ff_1_qn));  // open: preset, en, reset
  LED led_6 (.in(d_ff_2_q));
  D_Flip_Flop d_ff_2 (.clk(CLK), .D(nand_11_out), .Q(d_ff_2_q), .Qn(d_ff_2_qn));  // open: preset, en, reset

  // Notes on the sheet:
  //   `
  //   ^X1
  //   ^X0
  //   ^q1
  //   q1
  //   ^q0
  //   q0
  //   `
  //   J1
  //   J0
  //   y1
  //   y0
  //   q1
  //   q0
endmodule
