// Logisim project Pract7_2.circ as structural Verilog: 1 circuit, main circuit main
module main (
  input  CLK,
  input  X1,
  input  X0
);

  wire nor_1_out, nor_2_out, nor_3_out, nor_4_out, nor_5_out, nor_6_out, nor_7_out, s_r_ff_1_q, s_r_ff_1_qn,
       s_r_ff_2_q, s_r_ff_2_qn;

  nor nor_1 (nor_1_out, X1, X1);
  nor nor_2 (nor_2_out, X0, X0);
  nor nor_3 (nor_3_out, s_r_ff_1_q, nor_1_out);
  nor nor_4 (nor_4_out, s_r_ff_2_q, X1);
  nor nor_5 (nor_5_out, s_r_ff_1_q, s_r_ff_2_q);
  nor nor_6 (nor_6_out, nor_3_out, s_r_ff_2_q);
  LED led_1 (.in(nor_5_out));
  LED led_2 (.in(s_r_ff_1_q));
  not nor_7 (nor_7_out, nor_6_out);  // NOR_Gate
  LED led_3 (.in(nor_7_out));
  LED led_4 (.in(s_r_ff_1_q));
  LED led_5 (.in(nor_4_out));
  LED led_6 (.in(s_r_ff_2_q));
  LED led_7 (.in(s_r_ff_1_q));
  S_R_Flip_Flop s_r_ff_1 (
    .S(nor_7_out), .clk(CLK), .R(s_r_ff_1_q), .Q(s_r_ff_1_q), .Qn(s_r_ff_1_qn));  // open: preset, reset, en
  LED led_8 (.in(s_r_ff_2_q));
  S_R_Flip_Flop s_r_ff_2 (
    .S(nor_4_out), .clk(CLK), .R(s_r_ff_2_q), .Q(s_r_ff_2_q), .Qn(s_r_ff_2_qn));  // open: preset, reset, en

  // Notes on the sheet:
  //   `
  //   ^X1
  //   ^X0
  //   ^q1
  //   q1
  //   ^q0
  //   q0
  //   `
  //   S1
  //   R1
  //   S0
  //   R0
  //   y1
  //   y0
  //   q1
  //   q0
endmodule
