// Logisim project BUSHFIRE 17_1.circ as structural Verilog: 2 circuits, main circuit BUSHFIRE ROM
module BUSHFIRE_ROM (
  output a,
  output b,
  output c,
  output d,
  output e,
  output f,
  output g
);

  wire [2:0] clock_3_out;
  wire [7:7] rom_1_data;

  Clock #(.highDuration(2), .lowDuration(2)) clock_1 (.out(clock_3_out[1]));
  Clock #(.highDuration(4), .lowDuration(4)) clock_2 (.out(clock_3_out[2]));
  Clock clock_3 (.out(clock_3_out[0]));
  ROM #(.addrWidth(3)) rom_1 (.addr(clock_3_out), .data({rom_1_data[7], a, b, c, d, e, f, g}));  // open: sel
  _7_Segment_Display u_7_segment_display_1 (.g(g), .f(f), .a(a), .b(b), .e(e), .d(d), .c(c));  // open: dp

  // Notes on the sheet:
  //   BUSHFIRE ROM
  //   X1
  //   X2
  //   X0
  //   contents of rom_1 (hex, n*v repeats v):
  //   66 77 4e 37 30 5b 4f 5b
endmodule

module BUSHFIRE_POINTS (
  output a,
  output b,
  output c,
  output d,
  output e,
  output f,
  output g
);

  wire decoder_1_out0, decoder_1_out1, decoder_1_out2, decoder_1_out3, decoder_1_out4, decoder_1_out5,
       decoder_1_out6, decoder_1_out7;
  wire [2:0] clock_2_out;

  Clock #(.highDuration(2), .lowDuration(2)) clock_1 (.out(clock_2_out[1]));
  Clock clock_2 (.out(clock_2_out[0]));
  Clock #(.highDuration(4), .lowDuration(4)) clock_3 (.out(clock_2_out[2]));
  Decoder #(.select(3), .enable("false")) decoder_1 (
    .out0(decoder_1_out0), .out1(decoder_1_out1), .out2(decoder_1_out2), .out3(decoder_1_out3),
    .out4(decoder_1_out4), .out5(decoder_1_out5), .out6(decoder_1_out6), .out7(decoder_1_out7),
    .sel(clock_2_out));
  or or_1 (a, decoder_1_out2, decoder_1_out0, decoder_1_out1, decoder_1_out5, decoder_1_out6, decoder_1_out7);
  or or_2 (b, decoder_1_out0, decoder_1_out1, decoder_1_out3);
  or or_3 (c, decoder_1_out1, decoder_1_out3, decoder_1_out5, decoder_1_out7);
  or or_4 (e, decoder_1_out0, decoder_1_out1, decoder_1_out2, decoder_1_out3, decoder_1_out4, decoder_1_out6);
  or or_5 (f, decoder_1_out0, decoder_1_out1, decoder_1_out2, decoder_1_out3, decoder_1_out4, decoder_1_out5, decoder_1_out6, decoder_1_out7);
  or or_6 (g, decoder_1_out1, decoder_1_out3, decoder_1_out5, decoder_1_out6, decoder_1_out7);
  or or_7 (d, decoder_1_out5, decoder_1_out2, decoder_1_out7, decoder_1_out6);
  _7_Segment_Display u_7_segment_display_1 (.g(g), .f(f), .a(a), .b(b), .e(e), .d(d), .c(c));  // open: dp

  // Notes on the sheet:
  //   X2
  //   BUSHFIRE POINTS
  //   X1
  //   X0
endmodule
