// Logisim project 1.circ as structural Verilog: 1 circuit, main circuit main
module main (
  input  X2,
  input  X1,
  input  X0,
  output Y2,
  output Y1,
  output Y0
);

  wire and_1_out, and_2_out, and_3_out, and_4_out, and_5_out, and_6_out, and_7_out, and_8_out, nX0_out,
       nX1_out, nX2_out;

  not nX2 (nX2_out, X2);
  not nX1 (nX1_out, X1);
  not nX0 (nX0_out, X0);
  and and_1 (and_1_out, nX0_out, nX1_out);
  and and_2 (and_2_out, X0, X1);
  and and_3 (and_3_out, X2, nX0_out);
  and and_4 (and_4_out, X2, nX1_out);
  and and_5 (and_5_out, X1, nX0_out);
  and and_6 (and_6_out, nX2_out, X1);
  and and_7 (and_7_out, nX1_out, X0);
  and and_8 (and_8_out, nX2_out, X0);
  or or_1 (Y0, X2, nX0_out);
  or or_2 (Y1, and_1_out, X2, and_2_out);
  or or_3 (Y2, and_3_out, and_4_out, and_5_out, and_6_out, and_7_out, and_8_out);
endmodule
